// Digital circuit add_4.dig as structural Verilog
module add_4 (
  input  [3:0] x,
  input  [3:0] y,
  output [3:0] s
);

  wire full_add_1_c, full_add_2_c, half_add_1_c;

  half_add half_add_1 (.i0(x[0]), .i1(y[0]), .s(s[0]), .c(half_add_1_c));
  full_add full_add_1 (.i0(half_add_1_c), .i1(x[1]), .i2(y[1]), .s(s[1]), .c(full_add_1_c));
  full_add full_add_2 (.i0(full_add_1_c), .i1(x[2]), .i2(y[2]), .s(s[2]), .c(full_add_2_c));
  full_add full_add_3 (.i0(full_add_2_c), .i1(x[3]), .i2(y[3]), .s(s[3]));  // open: c
endmodule
