// Digital circuit alu_4.dig as structural Verilog
module alu_4 (
  input  [3:0] x,
  input  [3:0] y,
  input  [1:0] op,
  output [3:0] s,
  output zr
);

  wire [3:0] add_4_1_s, sub_4_1_s;

  add_4 add_4_1 (.x(x), .y(y), .s(add_4_1_s));
  sub_4 sub_4_1 (.x(x), .y(y), .s(sub_4_1_s));
  Multiplexer #(.Selector_Bits(2), .Bits(4)) multiplexer_1 (
    .sel(op), .in_0(x), .in_1(y), .in_2(add_4_1_s), .in_3(sub_4_1_s), .out(s));
  // zr_4 zr_4_1: pin names not known; wires that end beside it: s, zr

  // Notes on the sheet:
  //   op: op | out
  //   -------------
  //   00 | D+A
  //   01 | D-A
  //   10 | D&A
  //   11 | D|A
  //   c1c0 (op)
  //   --------
  //   00 |D
  //   01 |A
  //   10 |D+A
  //   11 | D-A
  //   is zero?
endmodule
