// Digital circuit counter_4.dig as structural Verilog
module counter_4 (
  input  load,
  input  [3:0] x,
  input  inc,
  input  clk,
  input  rst,
  output [3:0] s
);

  wire [3:0] inc_4_1_s, multiplexer_1_out, multiplexer_2_out, multiplexer_3_out;

  inc_4 inc_4_1 (.x(s), .s(inc_4_1_s));
  Multiplexer #(.Bits(4)) multiplexer_1 (.sel(inc), .in_0(s), .in_1(inc_4_1_s), .out(multiplexer_1_out));
  Multiplexer #(.Bits(4)) multiplexer_2 (.sel(load), .in_0(multiplexer_1_out), .in_1(x), .out(multiplexer_2_out));
  Multiplexer #(.Bits(4)) multiplexer_3 (.sel(rst), .in_0(multiplexer_2_out), .in_1(4'b0000), .out(multiplexer_3_out));
  reg_4 reg_4_1 (.in(multiplexer_3_out), .clk(clk), .load(1'b1), .out(s));

  // Notes on the sheet:
  //   s: output
endmodule
