// Digital circuit cpu_4.dig as structural Verilog
module cpu_4 (
  input  clk,
  input  [7:0] instr,
  input  [3:0] inM,
  input  rst,
  output [3:0] outM,
  output writeM,
  output [3:0] addrM
);

  wire a_dest, d_dest, JMP, m_dest, not_1_out, or_1_out, zr;
  wire [3:0] multiplexer_1_out, multiplexer_2_out, RegD_out;

  dest_decode dest_decode_1 (.d(instr[3:2]), .M(m_dest), .D_2(d_dest), .A(a_dest));  // open: NULL
  jmp_decode jmp_decode_1 (.j(instr[1:0]), .zr(zr), .JMP(JMP));
  Multiplexer #(.Bits(4)) multiplexer_1 (.sel(not_1_out), .in_0(outM), .in_1(instr[3:0]), .out(multiplexer_1_out));
  not not_1 (not_1_out, instr[7]);
  or or_1 (or_1_out, not_1_out, a_dest);
  reg_4 RegA (.in(multiplexer_1_out), .clk(clk), .load(or_1_out), .out(addrM));
  reg_4 RegD (.in(outM), .clk(clk), .load(d_dest), .out(RegD_out));
  counter_4 PC (.load(JMP), .x(addrM), .inc(1'b1), .clk(clk), .rst(rst));  // open: s
  Multiplexer #(.Bits(4)) multiplexer_2 (.sel(instr[6]), .in_0(addrM), .in_1(inM), .out(multiplexer_2_out));
  alu_4 ALU (.x(RegD_out), .y(multiplexer_2_out), .op(instr[5:4]), .s(outM), .zr(zr));
  and and_1 (writeM, instr[7], m_dest);

  // Other names for the same wires on the sheet: j[1:0] = instr[1:0]; v[3:0] = instr[3:0]; d[1:0] = instr[3:2];
  //   c[1:0] = instr[5:4]; a = instr[6]; i = instr[7]

  // Notes on the sheet:
  //   instr: 8 bit instruction
  //   A-ins: 0xxxvvvv
  //   C-ins: 1accddjj
  //   inM: RAM[A]
  //   writeM: write to the memory?
  //   addrM: at which address to write?
  //   8 bit instruction, last bit is i
  //   i=0 => A-ins: 0xxxvvvv
  //   i=1 => C-ins: 1accddjj
  //   A instruction:
  //   symbolic: @xx
  //   binary: 0vvvvvvv
  //   C instruction:
  //   symbolic: dest=comp;jump
  //   COMP
  //   for instructions like M=D etc..
  //   ALU should also be able to output D and A unchanged (also M, depending on the "a" bit which sets whether the second input of ALU should come from RegA or M )
  //   add/subtract is a must
  //   increments and decrements would also be nice?
  //   (for instructions like D=M+1)
  //   c1c0
  //   00 |D
  //   01 |A
  //   10 |D+A
  //   11| D-A
  //   again not sure about T.C.
  //   DEST
  //   we do need all the destinations, but not necessarily all at once?
  //   d1d0
  //   00 | null
  //   01 | M
  //   10 | D
  //   11 | A
  //   JUMP
  //   for turing completeness we need at least one conditional jump, idk about the rest. let's try:
  //   j1j0
  //   00 | no jump (so PC increments)
  //   01 | JUMP if 0 (ZR=1) 
  //   10 | JUMP if not 0 (ZR=0)
  //   11 | unconditional jump (like goto)
  //   idk if this is enough for TC tho.
  //   altogether can we get away with:
  //   A-ins: 0xxxvvvv
  //   C-ins: 1accddjj
  //   wow exactly 8 bits. let's go
  //   RegA should store when
  //   a-instr OR dest=a
  //   Write to memory if
  //   c-inst andd dest=M
endmodule
