// Digital circuit dest_decode.dig as structural Verilog
module dest_decode (
  input  [1:0] d,
  output NULL,
  output M,
  output D_2,
  output A
);

  wire not_1_out, not_2_out;

  not not_1 (not_1_out, d[1]);
  not not_2 (not_2_out, d[0]);
  and and_1 (NULL, not_2_out, not_1_out);
  and and_2 (M, d[0], not_1_out);
  and and_3 (D_2, not_2_out, d[1]);
  and and_4 (A, d[0], d[1]);

  // Notes on the sheet:
  //   d1d0
  //   00 | null
  //   01 | M
  //   10 | D
  //   11 | A
  //   gray-encoding
endmodule
