// Digital circuit jmp_decode.dig as structural Verilog
module jmp_decode (
  input  [1:0] j,
  input  zr,
  output JMP
);

  wire and_1_out, and_2_out, not_1_out;

  not not_1 (not_1_out, zr);
  and and_1 (and_1_out, j[0], zr);
  and and_2 (and_2_out, j[1], not_1_out);
  or or_1 (JMP, and_1_out, and_2_out);

  // Notes on the sheet:
  //   j1j0
  //   00 | no jump (so PC increments)
  //   01 | JUMP if 0 (ZR=1) 
  //   10 | JUMP if not 0 (ZR=0)
  //   11 | unconditional jump (like goto)
  //   thus
  //   j1 j0 zr | JMP
endmodule
