// Digital circuit reg_4.dig as structural Verilog
module reg_4 (
  input  [3:0] in,
  input  clk,
  input  load,
  output [3:0] out
);

  \bit  bit_1 (.d(in[0]), .l(load), .clk(clk), .q(out[0]));
  \bit  bit_2 (.d(in[1]), .l(load), .clk(clk), .q(out[1]));
  \bit  bit_3 (.d(in[2]), .l(load), .clk(clk), .q(out[2]));
  \bit  bit_4 (.d(in[3]), .l(load), .clk(clk), .q(out[3]));

  // Notes on the sheet:
  //   in: data
  //   load: load
  //   out: output
endmodule
