// Digital circuit sevseg.dig as structural Verilog
module sevseg (
  input  [3:0] x
);

  wire sevseg_driver_1_a, sevseg_driver_1_b, sevseg_driver_1_c, sevseg_driver_1_d, sevseg_driver_1_e,
       sevseg_driver_1_f, sevseg_driver_1_g;

  sevseg_driver sevseg_driver_1 (
    .i_0(x[0]), .i_1(x[1]), .i_2(x[2]), .i_3(x[3]), .a(sevseg_driver_1_a), .b(sevseg_driver_1_b),
    .c(sevseg_driver_1_c), .d(sevseg_driver_1_d), .e(sevseg_driver_1_e), .f(sevseg_driver_1_f),
    .g(sevseg_driver_1_g));
  Seven_Seg seven_seg_1 (
    .a(sevseg_driver_1_a), .b(sevseg_driver_1_b), .c(sevseg_driver_1_c), .d(sevseg_driver_1_d),
    .e(sevseg_driver_1_e), .f(sevseg_driver_1_f), .g(sevseg_driver_1_g), .dp(1'b0));
endmodule
