// Digital circuit sevseg_driver.dig as structural Verilog
module sevseg_driver (
  input  i_0,
  input  i_1,
  input  i_2,
  input  i_3,
  output a,
  output b,
  output c,
  output d,
  output e,
  output f,
  output g
);

  wire and_1_out, and_2_out, and_3_out, and_4_out, and_5_out, and_6_out, and_7_out, and_8_out, and_9_out,
       and_10_out, and_11_out, and_12_out, and_13_out, and_14_out, and_15_out, and_16_out, and_17_out,
       and_18_out, and_19_out, and_20_out, and_21_out, and_22_out, and_23_out, and_24_out, and_25_out,
       and_26_out, not_1_out, not_2_out, not_3_out, not_4_out;

  not not_1 (not_1_out, i_3);
  not not_2 (not_2_out, i_2);
  not not_3 (not_3_out, i_1);
  not not_4 (not_4_out, i_0);
  and and_1 (and_1_out, i_0, i_2, not_1_out);
  and and_2 (and_2_out, not_4_out, not_3_out, not_2_out);
  and and_3 (and_3_out, i_1, not_1_out);
  and and_4 (and_4_out, not_3_out, not_2_out, i_3);
  and and_5 (and_5_out, not_4_out, not_3_out, not_1_out);
  and and_6 (and_6_out, i_0, i_1, not_1_out);
  and and_7 (and_7_out, not_3_out, not_2_out);
  and and_8 (and_8_out, not_2_out, not_1_out);
  and and_9 (and_9_out, i_0, not_1_out);
  and and_10 (and_10_out, not_3_out, not_2_out);
  and and_11 (and_11_out, i_2, not_1_out);
  and and_12 (and_12_out, i_0, not_3_out, i_2, not_1_out);
  and and_13 (and_13_out, not_4_out, i_1, not_1_out);
  and and_14 (and_14_out, not_4_out, not_3_out, not_2_out);
  and and_15 (and_15_out, i_1, not_2_out, not_1_out);
  and and_16 (and_16_out, not_3_out, not_2_out, i_3);
  and and_17 (and_17_out, not_4_out, i_1, not_1_out);
  and and_18 (and_18_out, not_4_out, not_3_out, not_2_out);
  and and_19 (and_19_out, not_4_out, i_2, not_1_out);
  and and_20 (and_20_out, not_4_out, not_3_out, not_2_out);
  and and_21 (and_21_out, not_3_out, i_2, not_1_out);
  and and_22 (and_22_out, not_3_out, not_2_out, i_3);
  and and_23 (and_23_out, not_4_out, i_1, not_1_out);
  and and_24 (and_24_out, i_1, not_2_out, not_1_out);
  and and_25 (and_25_out, not_3_out, i_2, not_1_out);
  and and_26 (and_26_out, not_3_out, not_2_out, i_3);
  or or_1 (c, and_9_out, and_10_out, and_11_out);
  or or_2 (e, and_17_out, and_18_out);
  or or_3 (a, and_1_out, and_2_out, and_3_out, and_4_out);
  or or_4 (b, and_5_out, and_6_out, and_7_out, and_8_out);
  or or_5 (d, and_12_out, and_13_out, and_14_out, and_15_out, and_16_out);
  or or_6 (f, and_19_out, and_20_out, and_21_out, and_22_out);
  or or_7 (g, and_23_out, and_24_out, and_25_out, and_26_out);
endmodule
