// Digital circuit sub_4.dig as structural Verilog
module sub_4 (
  input  [3:0] x,
  input  [3:0] y,
  output [3:0] s
);

  wire [3:0] add_4_1_s, not_1_out;

  assign not_1_out = ~y;  // Not not_1, 4 bits wide
  add_4 add_4_1 (.x(not_1_out), .y(4'b0001), .s(add_4_1_s));
  add_4 add_4_2 (.x(x), .y(add_4_1_s), .s(s));

  // Notes on the sheet:
  //   y => -y
  //   invert y, add 1
endmodule
