// Digital circuit zr_4.dig as structural Verilog
module zr_4 (
  input  [15:0] x,
  output s
);

  wire nor_1_out, nor_2_out;

  nor nor_1 (nor_1_out, x[0], x[1]);
  nor nor_2 (nor_2_out, x[2], x[3]);
  and and_1 (s, nor_1_out, nor_2_out);
  // Pins of 4 and 16 bits meet at x
endmodule
