// Digital circuit add_16.dig as structural Verilog
module add_16 (
  input  [15:0] x,
  input  [15:0] y,
  output [15:0] s
);

  wire full_add_1_c, full_add_2_c, full_add_3_c, full_add_4_c, full_add_5_c, full_add_6_c, full_add_7_c,
       full_add_8_c, full_add_9_c, full_add_10_c, full_add_11_c, full_add_12_c, full_add_13_c, full_add_14_c,
       half_add_1_c;

  half_add half_add_1 (.i0(x[0]), .i1(y[0]), .s(s[0]), .c(half_add_1_c));
  full_add full_add_1 (.i0(half_add_1_c), .i1(x[1]), .i2(y[1]), .s(s[1]), .c(full_add_1_c));
  full_add full_add_2 (.i0(full_add_1_c), .i1(x[2]), .i2(y[2]), .s(s[2]), .c(full_add_2_c));
  full_add full_add_3 (.i0(full_add_2_c), .i1(x[3]), .i2(y[3]), .s(s[3]), .c(full_add_3_c));
  full_add full_add_4 (.i0(full_add_3_c), .i1(x[4]), .i2(y[4]), .s(s[4]), .c(full_add_4_c));
  full_add full_add_5 (.i0(full_add_4_c), .i1(x[5]), .i2(y[5]), .s(s[5]), .c(full_add_5_c));
  full_add full_add_6 (.i0(full_add_5_c), .i1(x[6]), .i2(y[6]), .s(s[6]), .c(full_add_6_c));
  full_add full_add_7 (.i0(full_add_6_c), .i1(x[7]), .i2(y[7]), .s(s[7]), .c(full_add_7_c));
  full_add full_add_8 (.i0(full_add_7_c), .i1(x[8]), .i2(y[8]), .s(s[8]), .c(full_add_8_c));
  full_add full_add_9 (.i0(full_add_8_c), .i1(x[9]), .i2(y[9]), .s(s[9]), .c(full_add_9_c));
  full_add full_add_10 (.i0(full_add_9_c), .i1(x[10]), .i2(y[10]), .s(s[10]), .c(full_add_10_c));
  full_add full_add_11 (.i0(full_add_10_c), .i1(x[11]), .i2(y[11]), .s(s[11]), .c(full_add_11_c));
  full_add full_add_12 (.i0(full_add_11_c), .i1(x[12]), .i2(y[12]), .s(s[12]), .c(full_add_12_c));
  full_add full_add_13 (.i0(full_add_12_c), .i1(x[13]), .i2(y[13]), .s(s[13]), .c(full_add_13_c));
  full_add full_add_14 (.i0(full_add_13_c), .i1(x[14]), .i2(y[14]), .s(s[14]), .c(full_add_14_c));
  full_add full_add_15 (.i0(full_add_14_c), .i1(x[15]), .i2(y[15]), .s(s[15]));  // open: c
endmodule
