// Digital circuit full_add.dig as structural Verilog
module full_add (
  input  i0,
  input  i1,
  input  i2,
  output s,
  output c
);

  wire half_add_1_c, half_add_1_s, half_add_2_c;

  half_add half_add_1 (.i0(i0), .i1(i1), .s(half_add_1_s), .c(half_add_1_c));
  half_add half_add_2 (.i0(half_add_1_s), .i1(i2), .s(s), .c(half_add_2_c));
  or or_1 (c, half_add_1_c, half_add_2_c);
endmodule
