// Digital circuit inc_16.dig as structural Verilog
module inc_16 (
  input  [15:0] x,
  output [15:0] s
);

  add_16 add_16_1 (.x(x), .y(16'h1), .s(s));
  // Pins of 1 and 16 bits meet at s

  // Notes on the sheet:
  //   x: input
  //   s: output = input + 1
endmodule
