// Digital circuit computer.dig as structural Verilog
module computer (
  input  clk,
  output [15:0] SCREEN
);

  computer #(.applicationType("IVERILOG"), .CodeFile("C:\\Users\\mirac\\Documents\\fpga\\nand2tetris\\cpu\\hack\\cpu.v")) u_computer (
    .clk(clk), .SCREEN(SCREEN));

  // Notes on the sheet:
  //   clk: Hz: 20
  //   1, 2, 3, 5, 8, 13, 21, 34, 55, 89, 144, 233, 377, 610, 987, 1597, 2584, 4181, 6765, 10946, 17711, 28657, 46368
endmodule
