// Digital circuit cpu.dig as structural Verilog
module cpu (
  input  clk,
  output [15:0] SCREEN
);

  wire [14:0] u_hack_pc;
  wire [15:0] ROM32K_d;

  ROM #(.AddrBits(15), .Bits(16)) ROM32K (.A(u_hack_pc), .sel(1'b1), .D(ROM32K_d));
  hack #(.applicationType("IVERILOG"), .CodeFile("C:\\Users\\mirac\\Documents\\fpga\\nand2tetris\\cpu_16bit\\hack\\hack.v")) u_hack (
    .instr(ROM32K_d), .clk(clk), .PC(u_hack_pc), .SCREEN(SCREEN));

  // Notes on the sheet:
  //   clk: Hz: 20
  //   1, 2, 3, 5, 8, 13, 21, 34, 55, 89, 144, 233, 377, 610, 987, 1597, 2584, 4181, 6765, 10946, 17711, 28657, 46368
  //   contents of ROM32K (hex, n*v repeats v):
  //   10,efc8,11,efc8,12,ea88,10,fc10,4000,e308,10,fc10,11,f090,12,e308
  //   ,10,fc10,11,e308,12,fc10,10,e308,6,ea87
endmodule
