// Digital circuit bcd.dig as structural Verilog
module bcd (
  input  [15:0] num,
  output [3:0] d1,
  output [3:0] d2,
  output [3:0] d3,
  output [3:0] d4
);

  bcd #(.applicationType("IVERILOG"), .CodeFile("bcd.v")) u_bcd (.bin(num), .bcd({d4, d3, d2, d1}));
endmodule
