// Digital circuit hack.dig as structural Verilog
module hack (
  input  btn1,
  input  clk_cpu,
  input  clk_disp,
  output a,
  output b,
  output c,
  output d,
  output e,
  output f,
  output g,
  output d4,
  output d3,
  output d2,
  output d1
);

  wire [1:0] counter_1_out;
  wire [3:0] multiplexer_1_out;
  wire [6:0] u_sevseg_pattern;
  wire [14:0] u_cpu_pc;
  wire [15:0] rom_d, u_bcd_bcd, u_cpu_screen;

  ROM #(.AddrBits(15), .Bits(16)) rom (.A(u_cpu_pc), .sel(1'b1), .D(rom_d));
  cpu #(.applicationType("IVERILOG"), .iverilogOptions("-I C:/Users/mirac/Documents/fpga/nand2tetris/cpu/hack/fpga"), .CodeFile("cpu.v")) u_cpu (
    .instr(rom_d), .clk(clk_cpu), .rstn(btn1), .PC(u_cpu_pc), .SCREEN(u_cpu_screen));
  bcd #(.applicationType("IVERILOG"), .CodeFile("bcd.v")) u_bcd (.bin(u_cpu_screen), .bcd(u_bcd_bcd));
  Counter #(.Bits(2)) counter_1 (.en(1'b1), .C(clk_disp), .clr(1'b0), .out(counter_1_out));  // open: ovf
  Multiplexer #(.Selector_Bits(2), .Bits(4)) multiplexer_1 (
    .sel(counter_1_out), .in_0(u_bcd_bcd[3:0]), .in_1(u_bcd_bcd[7:4]), .in_2(u_bcd_bcd[11:8]),
    .in_3(u_bcd_bcd[15:12]), .out(multiplexer_1_out));
  sevseg #(.applicationType("IVERILOG"), .CodeFile("sevseg.v")) u_sevseg (
    .in(multiplexer_1_out), .pattern(u_sevseg_pattern));
  assign {g, f, e, d, c, b, a} = ~u_sevseg_pattern;  // Not not_1, 7 bits wide
  Decoder #(.Selector_Bits(2)) decoder_1 (.sel(counter_1_out), .out_0(d1), .out_1(d2), .out_2(d3), .out_3(d4));

  // Notes on the sheet:
  //   clk_cpu: Hz: 20
  //   clk_disp: Hz: 120
  //   contents of rom (hex, n*v repeats v):
  //   10,efc8,11,efc8,12,ea88,10,fc10,f,e308,10,fc10,11,f090,12,e308
  //   ,10,fc10,11,e308,12,fc10,10,e308,6,ea87
endmodule
