// Digital circuit hack_fpga.dig as structural Verilog
module hack_fpga (
  input  clk,
  input  btn1,
  output a,
  output b,
  output c,
  output d,
  output e,
  output f,
  output g,
  output x0,
  output x1,
  output x2,
  output x3
);

  wire u_clkdiv20_clk_out, u_clkdiv120_clk_out;
  wire [1:0] counter_1_out;
  wire [3:0] multiplexer_1_out;
  wire [6:0] u_sevseg_pattern;
  wire [15:0] u_bcd_bcd, u_hack_screen;

  clkdiv20 #(.applicationType("IVERILOG"), .CodeFile("clkdiv20.v")) u_clkdiv20 (
    .clk(clk), .clk_out(u_clkdiv20_clk_out));
  hack #(.applicationType("IVERILOG"), .iverilogOptions("-I C:/Users/mirac/Documents/fpga/nand2tetris/cpu/hack/fpga"), .CodeFile("hack.v")) u_hack (
    .clk(u_clkdiv20_clk_out), .rstn(btn1), .SCREEN(u_hack_screen));
  bcd #(.applicationType("IVERILOG"), .CodeFile("bcd.v")) u_bcd (.bin(u_hack_screen), .bcd(u_bcd_bcd));
  clkdiv120 #(.applicationType("IVERILOG"), .CodeFile("clkdiv120.v")) u_clkdiv120 (
    .clk(clk), .clk_out(u_clkdiv120_clk_out));
  Counter #(.Bits(2)) counter_1 (.en(1'b1), .C(u_clkdiv120_clk_out), .clr(1'b0), .out(counter_1_out));  // open: ovf
  Multiplexer #(.Selector_Bits(2), .Bits(4)) multiplexer_1 (
    .sel(counter_1_out), .in_0(u_bcd_bcd[3:0]), .in_1(u_bcd_bcd[7:4]), .in_2(u_bcd_bcd[11:8]),
    .in_3(u_bcd_bcd[15:12]), .out(multiplexer_1_out));
  sevseg #(.applicationType("IVERILOG"), .CodeFile("sevseg.v")) u_sevseg (
    .in(multiplexer_1_out), .pattern(u_sevseg_pattern));
  assign {g, f, e, d, c, b, a} = ~u_sevseg_pattern;  // Not not_1, 7 bits wide
  Decoder #(.Selector_Bits(2)) decoder_1 (.sel(counter_1_out), .out_0(x0), .out_1(x1), .out_2(x2), .out_3(x3));

  // Notes on the sheet:
  //   clk: Hz: 2147483647
endmodule
