// Digital circuit hack_fpga_sevseg.dig as structural Verilog
module hack_fpga_sevseg (
  input  clk120,
  input  clk20
);

  wire hack_1_a, hack_1_b, hack_1_c, hack_1_d, hack_1_d1, hack_1_d2, hack_1_d3, hack_1_d4, hack_1_e,
       hack_1_f, hack_1_g;

  hack hack_1 (
    .btn1(1'b1), .clk_cpu(clk20), .clk_disp(clk120), .a(hack_1_a), .b(hack_1_b), .c(hack_1_c), .d(hack_1_d),
    .e(hack_1_e), .f(hack_1_f), .g(hack_1_g), .d4(hack_1_d4), .d3(hack_1_d3), .d2(hack_1_d2), .d1(hack_1_d1));
  Seven_Seg #(.commonConnectionType("anode"), .commonCathode("true"), .persistTime(10)) seven_seg_1 (
    .a(hack_1_a), .b(hack_1_b), .c(hack_1_c), .d(hack_1_d), .e(hack_1_e), .f(hack_1_f), .g(hack_1_g),
    .dp(1'b1), .common(hack_1_d4));
  Seven_Seg #(.commonCathode("true"), .commonConnectionType("anode"), .persistTime(10)) seven_seg_2 (
    .a(hack_1_a), .b(hack_1_b), .c(hack_1_c), .d(hack_1_d), .e(hack_1_e), .f(hack_1_f), .g(hack_1_g),
    .dp(1'b1), .common(hack_1_d3));
  Seven_Seg #(.commonCathode("true"), .commonConnectionType("anode"), .persistTime(10)) seven_seg_3 (
    .a(hack_1_a), .b(hack_1_b), .c(hack_1_c), .d(hack_1_d), .e(hack_1_e), .f(hack_1_f), .g(hack_1_g),
    .dp(1'b1), .common(hack_1_d2));
  Seven_Seg #(.commonCathode("true"), .commonConnectionType("anode"), .persistTime(10)) seven_seg_4 (
    .a(hack_1_a), .b(hack_1_b), .c(hack_1_c), .d(hack_1_d), .e(hack_1_e), .f(hack_1_f), .g(hack_1_g),
    .dp(1'b1), .common(hack_1_d1));

  // Notes on the sheet:
  //   clk120: Hz: 120
  //   clk20: Hz: 20
  //   0, 1, 2, 3, 5, 8, 13, 21, 34, 55, 89, 144, 233, 377, 610, 987, 1597, 2584, 4181, 6765
endmodule
