// Digital circuit rom.dig as structural Verilog
module rom (
  input  [14:0] addr,
  output [15:0] out
);

  ROM #(.applicationType("IVERILOG")) u_ROM (.A(addr), .D(out));
endmodule

/* Code of ROM:
module ROM (
    input [14:0] A,
    output reg [15:0] D
);
  reg [15:0] roma[0:255];

  initial begin
    $readmemh("fib.hex", roma);
  end

  always @(*) begin
    D = roma[A];
  end


endmodule
*/
