// Digital circuit sevseg.dig as structural Verilog
module sevseg (
  input  clk,
  input  clk_2
);

  wire decoder_1_out_0, decoder_1_out_1, decoder_1_out_2, decoder_1_out_3;
  wire [1:0] counter_1_out;
  wire [3:0] multiplexer_1_out, u_bcd_dig_1, u_bcd_dig_10, u_bcd_dig_100, u_bcd_dig_1000;
  wire [6:0] not_1_out, u_sevseg_pattern;
  wire [15:0] cpu_1_screen;

  cpu cpu_1 (.clk(clk_2), .SCREEN(cpu_1_screen));
  bcd #(.applicationType("IVERILOG"), .CodeFile("C:\\Users\\mirac\\Documents\\fpga\\nand2tetris\\cpu\\hack\\bcd.v")) u_bcd (
    .num(cpu_1_screen), .dig_1(u_bcd_dig_1), .dig_10(u_bcd_dig_10), .dig_100(u_bcd_dig_100),
    .dig_1000(u_bcd_dig_1000));
  Counter #(.Bits(2)) counter_1 (.en(1'b1), .C(clk), .clr(1'b0), .out(counter_1_out));  // open: ovf
  Multiplexer #(.Bits(4), .Selector_Bits(2)) multiplexer_1 (
    .sel(counter_1_out), .in_0(u_bcd_dig_1), .in_1(u_bcd_dig_10), .in_2(u_bcd_dig_100),
    .in_3(u_bcd_dig_1000), .out(multiplexer_1_out));
  sevseg #(.applicationType("IVERILOG"), .CodeFile("C:\\Users\\mirac\\Documents\\fpga\\nand2tetris\\cpu\\hack\\sevseg.v")) u_sevseg (
    .in(multiplexer_1_out), .pattern(u_sevseg_pattern));
  assign not_1_out = ~u_sevseg_pattern;  // Not not_1, 7 bits wide
  Seven_Seg #(.commonCathode("true"), .commonConnectionType("anode"), .persistTime(10)) seven_seg_1 (
    .a(not_1_out[0]), .b(not_1_out[1]), .c(not_1_out[2]), .d(not_1_out[3]), .e(not_1_out[4]),
    .f(not_1_out[5]), .g(not_1_out[6]), .dp(1'b1), .common(decoder_1_out_3));
  Decoder #(.Selector_Bits(2)) decoder_1 (
    .sel(counter_1_out), .out_0(decoder_1_out_0), .out_1(decoder_1_out_1), .out_2(decoder_1_out_2),
    .out_3(decoder_1_out_3));
  Seven_Seg #(.commonCathode("true"), .commonConnectionType("anode"), .persistTime(10)) seven_seg_2 (
    .a(not_1_out[0]), .b(not_1_out[1]), .c(not_1_out[2]), .d(not_1_out[3]), .e(not_1_out[4]),
    .f(not_1_out[5]), .g(not_1_out[6]), .dp(1'b1), .common(decoder_1_out_2));
  Seven_Seg #(.commonCathode("true"), .commonConnectionType("anode"), .persistTime(10)) seven_seg_3 (
    .a(not_1_out[0]), .b(not_1_out[1]), .c(not_1_out[2]), .d(not_1_out[3]), .e(not_1_out[4]),
    .f(not_1_out[5]), .g(not_1_out[6]), .dp(1'b1), .common(decoder_1_out_1));
  Seven_Seg #(.commonCathode("true"), .commonConnectionType("anode"), .persistTime(10)) seven_seg_4 (
    .a(not_1_out[0]), .b(not_1_out[1]), .c(not_1_out[2]), .d(not_1_out[3]), .e(not_1_out[4]),
    .f(not_1_out[5]), .g(not_1_out[6]), .dp(1'b1), .common(decoder_1_out_0));

  // Notes on the sheet:
  //   clk: Hz: 120
  //   clk_2: Hz: 20
endmodule
