// Digital circuit alu_16.dig as structural Verilog
module alu_16 (
  input  [5:0] op,
  input  [15:0] x,
  input  [15:0] y,
  output [15:0] s,
  output zr,
  output ng
);

  wire [15:0] add_16_1_s, and_1_out, multiplexer_1_out, multiplexer_2_out, multiplexer_3_out,
       multiplexer_4_out, multiplexer_5_out, not_1_out, not_2_out, not_3_out;

  Multiplexer #(.Bits(16)) multiplexer_1 (.sel(op[5]), .in_0(x), .in_1({16{1'b0}}), .out(multiplexer_1_out));
  Multiplexer #(.Bits(16)) multiplexer_2 (.sel(op[3]), .in_0(y), .in_1({16{1'b0}}), .out(multiplexer_2_out));
  assign not_1_out = ~multiplexer_1_out;  // Not not_1, 16 bits wide
  Multiplexer #(.Bits(16)) multiplexer_3 (
    .sel(op[4]), .in_0(multiplexer_1_out), .in_1(not_1_out), .out(multiplexer_3_out));
  Multiplexer #(.Bits(16)) multiplexer_4 (
    .sel(op[2]), .in_0(multiplexer_2_out), .in_1(not_2_out), .out(multiplexer_4_out));
  assign not_2_out = ~multiplexer_2_out;  // Not not_2, 16 bits wide
  assign and_1_out = multiplexer_3_out & multiplexer_4_out;  // And and_1, 16 bits wide
  add_16 add_16_1 (.x(multiplexer_3_out), .y(multiplexer_4_out), .s(add_16_1_s));
  Multiplexer #(.Bits(16)) multiplexer_5 (.sel(op[1]), .in_0(and_1_out), .in_1(add_16_1_s), .out(multiplexer_5_out));
  assign not_3_out = ~multiplexer_5_out;  // Not not_3, 16 bits wide
  Multiplexer #(.Bits(16)) multiplexer_6 (.sel(op[0]), .in_0(multiplexer_5_out), .in_1(not_3_out), .out(s));
  zr_16 zr_16_1 (.x(s), .s(zr));
  ng_16 ng_16_1 (.x(s), .s(ng));

  // Notes on the sheet:
  //   op: zx-nx-zy-ny-f-no
  //   zr: if out==0
  //   ng: if out<0
  //   zx
  //   zy
  //   nx
  //   ny
  //   f
  //   no
endmodule
