// Digital circuit zr_16.dig as structural Verilog
module zr_16 (
  input  [15:0] x,
  output s
);

  wire nor_1_out, nor_2_out, nor_3_out, nor_4_out, nor_5_out, nor_6_out, nor_7_out, nor_8_out;

  nor nor_1 (nor_1_out, x[0], x[1]);
  nor nor_2 (nor_2_out, x[2], x[3]);
  nor nor_3 (nor_3_out, x[4], x[5]);
  nor nor_4 (nor_4_out, x[6], x[7]);
  nor nor_5 (nor_5_out, x[8], x[9]);
  nor nor_6 (nor_6_out, x[10], x[11]);
  nor nor_7 (nor_7_out, x[12], x[13]);
  nor nor_8 (nor_8_out, x[14], x[15]);
  and and_1 (s, nor_1_out, nor_2_out, nor_3_out, nor_4_out, nor_5_out, nor_6_out, nor_7_out, nor_8_out);
endmodule
