// Digital circuit hack.dig as structural Verilog
module hack (
  input  clk,
  output [15:0] out_2
);

  wire [14:0] u_hack_pc;
  wire [15:0] ROM32K_d;

  ROM #(.AddrBits(15), .Bits(16)) ROM32K (.A(u_hack_pc), .sel(1'b1), .D(ROM32K_d));
  hack #(.applicationType("IVERILOG"), .CodeFile("C:\\Users\\mirac\\Documents\\fpga\\nand2tetris\\cpu_16bit\\hack\\hack.v")) u_hack (
    .instr(ROM32K_d), .clk(clk), .PC(u_hack_pc), .OUT(out_2));

  // Notes on the sheet:
  //   contents of ROM32K (hex, n*v repeats v):
  //   3,ec10,0,e308,4,ec10,1,e308,10,efc8,11,ea88,10,fc10,1,f4d0,1c
  //   ,e301,11,fc10,0,f090,11,e308,10,fdc8,c,ea87,11,fc10,1e,ea87
endmodule
