// Digital circuit jmp.dig as structural Verilog
module jmp (
  input  j0,
  input  j1,
  input  j2,
  input  ng,
  input  zr,
  output JMP
);

  wire and_1_out, and_2_out, and_3_out, and_4_out, not_1_out, not_2_out;

  not not_1 (not_1_out, ng);
  not not_2 (not_2_out, zr);
  and and_1 (and_1_out, j0, not_1_out, not_2_out);
  and and_2 (and_2_out, j0, j1, j2);
  and and_3 (and_3_out, j1, not_1_out, zr);
  and and_4 (and_4_out, j2, ng, not_2_out);
  or or_1 (JMP, and_1_out, and_2_out, and_3_out, and_4_out);

  // Notes on the sheet:
  //   How do we know if we have to effect a jump?
  //   The answer depends on the three j-bits of the
  //   current instruction and the two ALU output bits zr and ng.
  //   J2 | J1 | J0 | JMP
  //   ----------------------------------------
  //   0  | 0  |  0    | 0
  //   0  | 0  |  1    | comp > 0
  //   0  | 1  |  0    | comp = 0
  //   0  | 1  |  1    | comp >= 0
  //   1  | 0  |  0    | comp < 0
  //   1  | 0  |  1    | comp != 0
  //   1  | 1  |  0    | comp <= 0
  //   1  | 1  |  1    | 1
  //   JMP = (j0 !ng !zr) + (j1 !ng zr) + (j2 ng !zr) + (j0j1j2)
endmodule
