// Digital circuit counter_16.dig as structural Verilog
module counter_16 (
  input  [15:0] x,
  input  load,
  input  clk,
  input  inc,
  input  rst,
  output [15:0] s
);

  wire [15:0] inc_16_1_p2, multiplexer_1_out, multiplexer_2_out, multiplexer_3_out;

  // inc_16 inc_16_1: pin names not known; wires that end beside it: s, inc_16_1_p2
  Multiplexer #(.Bits(16)) multiplexer_1 (.sel(inc), .in_0(s), .in_1(inc_16_1_p2), .out(multiplexer_1_out));
  Multiplexer #(.Bits(16)) multiplexer_2 (.sel(load), .in_0(multiplexer_1_out), .in_1(x), .out(multiplexer_2_out));
  Multiplexer #(.Bits(16)) multiplexer_3 (
    .sel(rst), .in_0(multiplexer_2_out), .in_1({16{1'b0}}), .out(multiplexer_3_out));
  // reg_16 reg_16_1: pin names not known; wires that end beside it: multiplexer_3_out, 1'b1, clk, s

  // Notes on the sheet:
  //   s: output
endmodule
