// Digital circuit ram16k_orig.dig as structural Verilog
module ram16k_orig (
  input  [15:0] d,
  input  rw,
  input  [13:0] a,
  input  clk,
  output [15:0] q
);

  wire demultiplexer_1_out_0, demultiplexer_1_out_1, demultiplexer_1_out_2, demultiplexer_1_out_3;
  wire [15:0] ram4k_1_q, ram4k_2_q, ram4k_3_q, ram4k_4_q;

  Demultiplexer #(.Selector_Bits(2)) demultiplexer_1 (
    .sel(a[13:12]), .in(rw), .out_0(demultiplexer_1_out_0), .out_1(demultiplexer_1_out_1),
    .out_2(demultiplexer_1_out_2), .out_3(demultiplexer_1_out_3));
  ram4k ram4k_1 (.d(d), .rw(demultiplexer_1_out_0), .a(a[11:0]), .clk(clk), .q(ram4k_1_q));
  ram4k ram4k_2 (.d(d), .rw(demultiplexer_1_out_1), .a(a[11:0]), .clk(clk), .q(ram4k_2_q));
  ram4k ram4k_3 (.d(d), .rw(demultiplexer_1_out_2), .a(a[11:0]), .clk(clk), .q(ram4k_3_q));
  ram4k ram4k_4 (.d(d), .rw(demultiplexer_1_out_3), .a(a[11:0]), .clk(clk), .q(ram4k_4_q));
  Multiplexer #(.Selector_Bits(2), .Bits(16)) multiplexer_1 (
    .sel(a[13:12]), .in_0(ram4k_1_q), .in_1(ram4k_2_q), .in_2(ram4k_3_q), .in_3(ram4k_4_q), .out(q));

  // Notes on the sheet:
  //   d: data
  //   q: output[16]
  //   rw: read = 0, write = 1
  //   a: address[14]
endmodule
