// Digital circuit ram4k.dig as structural Verilog
module ram4k (
  input  [15:0] d,
  input  rw,
  input  [11:0] a,
  input  clk,
  output [15:0] q
);

  wire demultiplexer_1_out_0, demultiplexer_1_out_1, demultiplexer_1_out_2, demultiplexer_1_out_3,
       demultiplexer_1_out_4, demultiplexer_1_out_5, demultiplexer_1_out_6, demultiplexer_1_out_7;
  wire [15:0] ram512_1_q, ram512_2_q, ram512_3_q, ram512_4_q, ram512_5_q, ram512_6_q, ram512_7_q, ram512_8_q;

  Demultiplexer #(.Selector_Bits(3)) demultiplexer_1 (
    .sel(a[11:9]), .in(rw), .out_0(demultiplexer_1_out_0), .out_1(demultiplexer_1_out_1),
    .out_2(demultiplexer_1_out_2), .out_3(demultiplexer_1_out_3), .out_4(demultiplexer_1_out_4),
    .out_5(demultiplexer_1_out_5), .out_6(demultiplexer_1_out_6), .out_7(demultiplexer_1_out_7));
  ram512 ram512_1 (.d(d), .rw(demultiplexer_1_out_0), .a(a[8:0]), .clk(clk), .q(ram512_1_q));
  ram512 ram512_2 (.d(d), .rw(demultiplexer_1_out_1), .a(a[8:0]), .clk(clk), .q(ram512_2_q));
  ram512 ram512_3 (.d(d), .rw(demultiplexer_1_out_2), .a(a[8:0]), .clk(clk), .q(ram512_3_q));
  ram512 ram512_4 (.d(d), .rw(demultiplexer_1_out_3), .a(a[8:0]), .clk(clk), .q(ram512_4_q));
  ram512 ram512_5 (.d(d), .rw(demultiplexer_1_out_4), .a(a[8:0]), .clk(clk), .q(ram512_5_q));
  ram512 ram512_6 (.d(d), .rw(demultiplexer_1_out_5), .a(a[8:0]), .clk(clk), .q(ram512_6_q));
  ram512 ram512_7 (.d(d), .rw(demultiplexer_1_out_6), .a(a[8:0]), .clk(clk), .q(ram512_7_q));
  ram512 ram512_8 (.d(d), .rw(demultiplexer_1_out_7), .a(a[8:0]), .clk(clk), .q(ram512_8_q));
  Multiplexer #(.Selector_Bits(3), .Bits(16)) multiplexer_1 (
    .sel(a[11:9]), .in_0(ram512_1_q), .in_1(ram512_2_q), .in_2(ram512_3_q), .in_3(ram512_4_q),
    .in_4(ram512_5_q), .in_5(ram512_6_q), .in_6(ram512_7_q), .in_7(ram512_8_q), .out(q));

  // Notes on the sheet:
  //   d: data
  //   q: output[16]
  //   rw: read = 0, write = 1
  //   a: address[12]
endmodule
