// Digital circuit ram64.dig as structural Verilog
module ram64 (
  input  [15:0] d,
  input  rw,
  input  [5:0] a,
  input  clk,
  output [15:0] q
);

  wire demultiplexer_1_out_0, demultiplexer_1_out_1, demultiplexer_1_out_2, demultiplexer_1_out_3,
       demultiplexer_1_out_4, demultiplexer_1_out_5, demultiplexer_1_out_6, demultiplexer_1_out_7;
  wire [15:0] ram8_1_out, ram8_2_out, ram8_3_out, ram8_4_out, ram8_5_out, ram8_6_out, ram8_7_out, ram8_8_out;

  Demultiplexer #(.Selector_Bits(3)) demultiplexer_1 (
    .sel(a[5:3]), .in(rw), .out_0(demultiplexer_1_out_0), .out_1(demultiplexer_1_out_1),
    .out_2(demultiplexer_1_out_2), .out_3(demultiplexer_1_out_3), .out_4(demultiplexer_1_out_4),
    .out_5(demultiplexer_1_out_5), .out_6(demultiplexer_1_out_6), .out_7(demultiplexer_1_out_7));
  ram8 ram8_1 (.data(d), .rw(demultiplexer_1_out_0), .addr(a[2:0]), .clk(clk), .out(ram8_1_out));
  ram8 ram8_2 (.data(d), .rw(demultiplexer_1_out_1), .addr(a[2:0]), .clk(clk), .out(ram8_2_out));
  ram8 ram8_3 (.data(d), .rw(demultiplexer_1_out_2), .addr(a[2:0]), .clk(clk), .out(ram8_3_out));
  ram8 ram8_4 (.data(d), .rw(demultiplexer_1_out_3), .addr(a[2:0]), .clk(clk), .out(ram8_4_out));
  ram8 ram8_5 (.data(d), .rw(demultiplexer_1_out_4), .addr(a[2:0]), .clk(clk), .out(ram8_5_out));
  ram8 ram8_6 (.data(d), .rw(demultiplexer_1_out_5), .addr(a[2:0]), .clk(clk), .out(ram8_6_out));
  ram8 ram8_7 (.data(d), .rw(demultiplexer_1_out_6), .addr(a[2:0]), .clk(clk), .out(ram8_7_out));
  ram8 ram8_8 (.data(d), .rw(demultiplexer_1_out_7), .addr(a[2:0]), .clk(clk), .out(ram8_8_out));
  Multiplexer #(.Selector_Bits(3), .Bits(16)) multiplexer_1 (
    .sel(a[5:3]), .in_0(ram8_1_out), .in_1(ram8_2_out), .in_2(ram8_3_out), .in_3(ram8_4_out),
    .in_4(ram8_5_out), .in_5(ram8_6_out), .in_6(ram8_7_out), .in_7(ram8_8_out), .out(q));

  // Notes on the sheet:
  //   d: data
  //   q: output[16]
  //   rw: read = 0, write = 1
  //   a: address[6]
endmodule
