// Digital circuit bit.dig as structural Verilog
module \bit  (
  input  d,
  input  rw,
  input  clk,
  output q
);

  wire multiplexer_1_out;

  Multiplexer multiplexer_1 (.sel(rw), .in_0(q), .in_1(d), .out(multiplexer_1_out));
  D_FF d_ff_1 (.D(multiplexer_1_out), .C(clk), .Q(q));  // open: nQ

  // Notes on the sheet:
  //   d: data
  //   rw: load
  //   q: output
endmodule
