// Digital circuit computer.dig as structural Verilog
module computer (
  input  clk,
  input  reset,
  output [15:0] A,
  output [15:0] D
);

  wire cpu_1_writem;
  wire [14:0] cpu_1_addrm, cpu_1_pc;
  wire [15:0] blockramdualport_1_d, cpu_1_outm, ROM32K_d;

  ROM #(.AddrBits(15), .Bits(16)) ROM32K (.A(cpu_1_pc), .sel(1'b1), .D(ROM32K_d));
  cpu cpu_1 (
    .inM(blockramdualport_1_d), .instr(ROM32K_d), .rst(reset), .clk(clk), .addrM(cpu_1_addrm),
    .outM(cpu_1_outm), .writeM(cpu_1_writem), .PC(cpu_1_pc), .RegA(A), .RegD(D));
  BlockRAMDualPort #(.AddrBits(15), .isProgramMemory("true"), .Bits(16)) blockramdualport_1 (
    .A(cpu_1_addrm), .Din(cpu_1_outm), .str(cpu_1_writem), .C(clk), .D(blockramdualport_1_d));

  // Notes on the sheet:
  //   contents of ROM32K (hex, n*v repeats v):
  //   3,ec10,0,e308,4,ec10,1,e308,0,fc10,1,f090,2,e308
endmodule
