// Digital circuit cpu.dig as structural Verilog
module cpu (
  input  [15:0] inM,
  input  [15:0] instr,
  input  rst,
  input  clk,
  output [14:0] addrM,
  output [15:0] outM,
  output writeM,
  output [14:0] PC,
  output [15:0] RegA,
  output [15:0] RegD
);

  wire and_1_out, jmp_1_jmp, ng, not_1_out, or_1_out, zr;
  wire [15:0] multiplexer_1_out, multiplexer_2_out;
  wire [15:15] PC_s;

  Multiplexer #(.Bits(16)) multiplexer_1 (.sel(not_1_out), .in_0(outM), .in_1(instr), .out(multiplexer_1_out));
  or or_1 (or_1_out, not_1_out, instr[5]);
  not not_1 (not_1_out, instr[15]);
  // reg_16 RegA: pin names not known; wires that end beside it: multiplexer_1_out, clk, or_1_out, {RegA[15], addrM}
  counter_16 u_PC (.x({RegA[15], addrM}), .load(and_1_out), .clk(clk), .inc(1'b1), .rst(rst), .s({PC_s[15], PC}));
  Multiplexer #(.Bits(16)) multiplexer_2 (
    .sel(instr[12]), .in_0({RegA[15], addrM}), .in_1(inM), .out(multiplexer_2_out));
  and and_1 (and_1_out, instr[15], jmp_1_jmp);
  // reg_16 RegD: pin names not known; wires that end beside it: outM, clk, instr[4], RegD
  alu_16 ALU (.op(instr[11:6]), .x(RegD), .y(multiplexer_2_out), .s(outM), .zr(zr), .ng(ng));
  jmp jmp_1 (.j0(instr[0]), .j1(instr[1]), .j2(instr[2]), .ng(ng), .zr(zr), .JMP(jmp_1_jmp));
  and and_2 (writeM, instr[15], instr[3]);

  assign RegA[14:0] = addrM;

  // Other names for the same wires on the sheet: j[2:0] = instr[2:0]; d[2:0] = instr[5:3]; d0 = instr[3];
  //   d1 = instr[4]; d2 = instr[5]; c[5:0] = instr[11:6]; a = instr[12]; ac = instr[15]

  // Notes on the sheet:
  //   inM: instruction's M input, contents of RAM[A]
  //   addrM: at which address to write?
  //   outM: written to RAM[addressM], instruction's M output
  //   writeM: write to the memory?
  //   PC: address of next instr
  //   instruction decoding
  //   In case of an A-instruction, the instruction bits are interpreted as a binary value that should be loaded
  //   into the A register. In case of a C-instruction, the instruction is treated as a
  //   capsule of control bits 1xxaccccccdddjjj, as follows. The a and cccccc bits code
  //   the comp part of the instruction; the ddd bits code the dest part of the
  //   instruction; the jjj bits code the jump part of the instruction. The xx bits are ignored.
  //   if a = 0, ALU'S y comes from A
  //   if a =1 it comes from memory via inM
  //   ac = 0 => a-instr
  //   ac = 1 => c-instr
  //   d2 d1 d0 | dest
  //   ---------|------
  //   0  0  0  | null
  //   0  0  1  | RAM[A] (M)
  //   0  1  0  | D
  //   0  1  1  | DM
  //   1  0  0  | A
  //   1  0  1  | AM
  //   1  1  0  | AD
  //   1  1  1  | ADM
  //   a-instr or c-instr
  //   in effect, whether to store:
  //   d0 => M, d1 => D, d2 => A
  //   ALSO when a-instr
  //   RegA should store
  //   if jump: PC=A else: PC++, thus:
  //   J | inc | load
  //   --------------
  //   0 | 0 | 1
  //   1 | 1 | 0
  //   ignore the ac (MSB)
  //   jump
endmodule
