// Digital circuit jmp.dig as structural Verilog
module jmp (
  input  zr,
  input  ng,
  input  [2:0] j,
  output JMP
);

  wire and_1_out, and_2_out, and_3_out, not_1_out;

  and and_1 (and_1_out, not_1_out, j[0]);
  not not_1 (not_1_out, ng);
  and and_2 (and_2_out, zr, j[1]);
  and and_3 (and_3_out, ng, j[2]);
  or or_1 (JMP, and_1_out, and_2_out, and_3_out);

  // Notes on the sheet:
  //   How do we know if we have to effect a jump?
  //   The answer depends on the three j-bits of the
  //   current instruction and the two ALU output bits zr and ng.
  //   J2 | J1 | J0 | JMP
  //   ----------------------------------------
  //   0  | 0  |  0    | 0
  //   0  | 0  |  1    | comp > 0
  //   0  | 1  |  0    | comp = 0
  //   0  | 1  |  1    | comp >= 0
  //   1  | 0  |  0    | comp < 0
  //   1  | 0  |  1    | comp != 0
  //   1  | 1  |  0    | comp <= 0
  //   1  | 1  |  1    | 1
  //   JMP = J0!NG or J1ZR or J2NG
endmodule
