// Digital circuit mem.dig as structural Verilog
module mem (
  input  [15:0] in,
  input  [14:0] addr,
  input  load,
  input  clk,
  output [15:0] out
);

  BlockRAMDualPort #(.AddrBits(15), .Bits(16)) blockramdualport_1 (.A(addr), .Din(in), .str(load), .C(clk), .D(out));
endmodule
