// Digital circuit ram16k.dig as structural Verilog
module ram16k (
  input  [15:0] d,
  input  rw,
  input  [13:0] a,
  input  clk,
  output [15:0] q
);

  wire demultiplexer_1_out_0, demultiplexer_1_out_1, demultiplexer_1_out_2, demultiplexer_1_out_3;
  wire [15:0] ram4k_2_d, ram4k_3_d, ram4k_4_d, ram4k_d;

  Demultiplexer #(.Selector_Bits(2)) demultiplexer_1 (
    .sel(a[13:12]), .in(rw), .out_0(demultiplexer_1_out_0), .out_1(demultiplexer_1_out_1),
    .out_2(demultiplexer_1_out_2), .out_3(demultiplexer_1_out_3));
  BlockRAMDualPort #(.AddrBits(12), .Bits(16)) ram4k (
    .A(a[11:0]), .Din(d), .str(demultiplexer_1_out_0), .C(clk), .D(ram4k_d));
  BlockRAMDualPort #(.AddrBits(12), .Bits(16)) ram4k_2 (
    .A(a[11:0]), .Din(d), .str(demultiplexer_1_out_1), .C(clk), .D(ram4k_2_d));
  BlockRAMDualPort #(.AddrBits(12), .Bits(16)) ram4k_3 (
    .A(a[11:0]), .Din(d), .str(demultiplexer_1_out_2), .C(clk), .D(ram4k_3_d));
  BlockRAMDualPort #(.AddrBits(12), .Bits(16)) ram4k_4 (
    .A(a[11:0]), .Din(d), .str(demultiplexer_1_out_3), .C(clk), .D(ram4k_4_d));
  Multiplexer #(.Selector_Bits(2), .Bits(16)) multiplexer_1 (
    .sel(a[13:12]), .in_0(ram4k_d), .in_1(ram4k_2_d), .in_2(ram4k_3_d), .in_3(ram4k_4_d), .out(q));

  // Notes on the sheet:
  //   d: data
  //   q: output[16]
  //   rw: read = 0, write = 1
  //   a: address[14]
endmodule
