// Digital circuit ram512.dig as structural Verilog
module ram512 (
  input  [15:0] d,
  input  rw,
  input  [8:0] a,
  input  clk,
  output [15:0] q
);

  wire demultiplexer_1_out_0, demultiplexer_1_out_1, demultiplexer_1_out_2, demultiplexer_1_out_3,
       demultiplexer_1_out_4, demultiplexer_1_out_5, demultiplexer_1_out_6, demultiplexer_1_out_7;
  wire [15:0] ram64_1_q, ram64_2_q, ram64_3_q, ram64_4_q, ram64_5_q, ram64_6_q, ram64_7_q, ram64_8_q;

  Demultiplexer #(.Selector_Bits(3)) demultiplexer_1 (
    .sel(a[8:6]), .in(rw), .out_0(demultiplexer_1_out_0), .out_1(demultiplexer_1_out_1),
    .out_2(demultiplexer_1_out_2), .out_3(demultiplexer_1_out_3), .out_4(demultiplexer_1_out_4),
    .out_5(demultiplexer_1_out_5), .out_6(demultiplexer_1_out_6), .out_7(demultiplexer_1_out_7));
  ram64 ram64_1 (.d(d), .rw(demultiplexer_1_out_0), .a(a[5:0]), .clk(clk), .q(ram64_1_q));
  ram64 ram64_2 (.d(d), .rw(demultiplexer_1_out_1), .a(a[5:0]), .clk(clk), .q(ram64_2_q));
  ram64 ram64_3 (.d(d), .rw(demultiplexer_1_out_2), .a(a[5:0]), .clk(clk), .q(ram64_3_q));
  ram64 ram64_4 (.d(d), .rw(demultiplexer_1_out_3), .a(a[5:0]), .clk(clk), .q(ram64_4_q));
  ram64 ram64_5 (.d(d), .rw(demultiplexer_1_out_4), .a(a[5:0]), .clk(clk), .q(ram64_5_q));
  ram64 ram64_6 (.d(d), .rw(demultiplexer_1_out_5), .a(a[5:0]), .clk(clk), .q(ram64_6_q));
  ram64 ram64_7 (.d(d), .rw(demultiplexer_1_out_6), .a(a[5:0]), .clk(clk), .q(ram64_7_q));
  ram64 ram64_8 (.d(d), .rw(demultiplexer_1_out_7), .a(a[5:0]), .clk(clk), .q(ram64_8_q));
  Multiplexer #(.Selector_Bits(3), .Bits(16)) multiplexer_1 (
    .sel(a[8:6]), .in_0(ram64_1_q), .in_1(ram64_2_q), .in_2(ram64_3_q), .in_3(ram64_4_q), .in_4(ram64_5_q),
    .in_5(ram64_6_q), .in_6(ram64_7_q), .in_7(ram64_8_q), .out(q));

  // Notes on the sheet:
  //   d: data
  //   q: output[16]
  //   rw: read = 0, write = 1
  //   a: address[9]
endmodule
