// Digital circuit ram8.dig as structural Verilog
module ram8 (
  input  [15:0] data,
  input  rw,
  input  [2:0] addr,
  input  clk,
  output [15:0] out
);

  wire demultiplexer_1_out_0, demultiplexer_1_out_1, demultiplexer_1_out_2, demultiplexer_1_out_3,
       demultiplexer_1_out_4, demultiplexer_1_out_5, demultiplexer_1_out_6, demultiplexer_1_out_7;
  wire [15:0] reg_16_1_p4, reg_16_2_p4, reg_16_3_p4, reg_16_4_p4, reg_16_5_p4, reg_16_6_p4, reg_16_7_p4,
       reg_16_8_p4;

  Demultiplexer #(.Selector_Bits(3)) demultiplexer_1 (
    .sel(addr), .in(rw), .out_0(demultiplexer_1_out_0), .out_1(demultiplexer_1_out_1),
    .out_2(demultiplexer_1_out_2), .out_3(demultiplexer_1_out_3), .out_4(demultiplexer_1_out_4),
    .out_5(demultiplexer_1_out_5), .out_6(demultiplexer_1_out_6), .out_7(demultiplexer_1_out_7));
  // reg_16 reg_16_1: pin names not known; wires that end beside it: data, demultiplexer_1_out_0, clk, reg_16_1_p4
  // reg_16 reg_16_2: pin names not known; wires that end beside it: data, demultiplexer_1_out_1, clk, reg_16_2_p4
  // reg_16 reg_16_3: pin names not known; wires that end beside it: data, demultiplexer_1_out_2, clk, reg_16_3_p4
  // reg_16 reg_16_4: pin names not known; wires that end beside it: data, demultiplexer_1_out_3, clk, reg_16_4_p4
  // reg_16 reg_16_5: pin names not known; wires that end beside it: data, demultiplexer_1_out_4, clk, reg_16_5_p4
  // reg_16 reg_16_6: pin names not known; wires that end beside it: data, demultiplexer_1_out_5, clk, reg_16_6_p4
  // reg_16 reg_16_7: pin names not known; wires that end beside it: data, demultiplexer_1_out_6, clk, reg_16_7_p4
  // reg_16 reg_16_8: pin names not known; wires that end beside it: data, demultiplexer_1_out_7, clk, reg_16_8_p4
  Multiplexer #(.Selector_Bits(3), .Bits(16)) multiplexer_1 (
    .sel(addr), .in_0(reg_16_1_p4), .in_1(reg_16_2_p4), .in_2(reg_16_3_p4), .in_3(reg_16_4_p4),
    .in_4(reg_16_5_p4), .in_5(reg_16_6_p4), .in_6(reg_16_7_p4), .in_7(reg_16_8_p4), .out(out));

  // Notes on the sheet:
  //   out: output[16]
  //   data: data
  //   rw: read = 0, write = 1
  //   addr: address[3]
endmodule
