// Digital circuit reg_16.dig as structural Verilog
module reg_16 (
  input  [15:0] in,
  input  clk,
  input  load,
  output [15:0] out
);

  \bit  bit_1 (.d(in[0]), .rw(load), .clk(clk), .q(out[0]));
  \bit  bit_2 (.d(in[1]), .rw(load), .clk(clk), .q(out[1]));
  \bit  bit_3 (.d(in[2]), .rw(load), .clk(clk), .q(out[2]));
  \bit  bit_4 (.d(in[3]), .rw(load), .clk(clk), .q(out[3]));
  \bit  bit_5 (.d(in[4]), .rw(load), .clk(clk), .q(out[4]));
  \bit  bit_6 (.d(in[5]), .rw(load), .clk(clk), .q(out[5]));
  \bit  bit_7 (.d(in[6]), .rw(load), .clk(clk), .q(out[6]));
  \bit  bit_8 (.d(in[7]), .rw(load), .clk(clk), .q(out[7]));
  \bit  bit_9 (.d(in[8]), .rw(load), .clk(clk), .q(out[8]));
  \bit  bit_10 (.d(in[9]), .rw(load), .clk(clk), .q(out[9]));
  \bit  bit_11 (.d(in[10]), .rw(load), .clk(clk), .q(out[10]));
  \bit  bit_12 (.d(in[11]), .rw(load), .clk(clk), .q(out[11]));
  \bit  bit_13 (.d(in[12]), .rw(load), .clk(clk), .q(out[12]));
  \bit  bit_14 (.d(in[13]), .rw(load), .clk(clk), .q(out[13]));
  \bit  bit_15 (.d(in[14]), .rw(load), .clk(clk), .q(out[14]));
  \bit  bit_16 (.d(in[15]), .rw(load), .clk(clk), .q(out[15]));

  // Notes on the sheet:
  //   in: data
  //   load: load
  //   out: output
endmodule
